# Fritzing sketch TrainMovementMeasurer (saved by Fritzing 0.9.4)
breadboards: 2

parts:
  R1 = Resistor [tolerance=±5% resistance=820 package=THT]
  Part1 = Arduino Nano (Rev3.0)
  R2 = Resistor [tolerance=±5% resistance=470 package=THT]
  R3 = Resistor [tolerance=±5% resistance=470 package=THT]
  R4 = Resistor [tolerance=±5% resistance=470 package=THT]
  R5 = Resistor [tolerance=±5% resistance=18 package=THT]
  C2 = Ceramic Capacitor [capacitance=470nF package="100 mil [THT, multilayer]"]
  C3 = Ceramic Capacitor [capacitance=470nF package="100 mil [THT, multilayer]"]
  LED1 = LED - 5mm [color="Infrared (940nm)" package="5 mm [THT]"]
  LED2 = LED - 5mm [color="Infrared (940nm)" package="5 mm [THT]"]
  LED3 = LED - 5mm [color="Infrared (940nm)" package="5 mm [THT]"]
  R7 = Resistor [tolerance=±5% resistance=18 power=1W package=THT]
  R6 = Resistor [tolerance=±5% resistance=18 package=THT]
  T1 = NPN-Transistor [part_number=TIP31C package="TO92 [THT]"]
  J4 = Screw terminal - 2 pins [package=THT]
  C1 = Ceramic Capacitor [capacitance=470nF package="100 mil [THT, multilayer]"]
  J2B = female pin header, 2 pins [form="♀ (female)"]
  J1 = single row smd female pin header, 4 pins [form="♀ (female)"]
  J2A = single row smd female pin header, 5 pins [form="♀ (female)"]
  J3 = single row smd male pin header, 3 pins [form="♂ (male)"]

nets:
  N1: R1.Pin_0, Part1.D11/MOSI
  N2: R1.Pin_1, T1.B
  N3: Part1.GND, C2.0, C3.0, T1.E, J4.pin1, C1.0, J1.pin4, J2A.pin4, J3.pin1
  N4: Part1.D3, R4.Pin_1, J2A.pin3
  N5: Part1.D4, R3.Pin_1, J2A.pin2
  N6: Part1.D5, R2.Pin_1, J2A.pin1
  N7: Part1.D12/MISO, J3.pin2
  N8: Part1.VIN, J4.pin2
  N9: Part1.5V, R5.Pin_0, R7.Pin_0, R6.Pin_0, J2B.pin1, J1.pin3, J2A.pin5, J3.pin3
  N10: Part1.A5, J1.pin2
  N11: Part1.A4, J1.pin1
  N12: R2.Pin_0, C1.1
  N13: R3.Pin_0, C2.1
  N14: R4.Pin_0, C3.1
  N15: R5.Pin_1, LED1.anode
  N16: LED1.cathode, LED2.cathode, LED3.cathode, T1.C, J2B.pin2
  N17: LED2.anode, R6.Pin_1
  N18: LED3.anode, R7.Pin_1

notes:
  Pwr
  Screen
  If the IR LEDs are not required to have a 38KHz carrier then T1 (a TIP31C) and R1 (820Ω) may be ommitted and the LEDs are connected directly to both power busses.
  Or the GATE_LED_CONSTANT #define must be set in the code.
  The strip of WS2812 LEDs is optional. If absent the code must stil be configured to output to at least 8 of them. The absence of the actual LEDs will do no harm.
  Note the large number of empty breadboard lines here, to allow you to change wire positions as your screen requires.
  I2C Connection to Display
  Power In
  3 x Light Gate Detectors
  3 x Light Gate Emitters
  Detectors
  LED Stick
